# Fritzing sketch Projeto-Temperatura-Umidade (saved by Fritzing 0.9.3b)
breadboards: 1

parts:
  Arduino_Uno = Arduino Uno (Rev3)
  HC-05 = Bluetooth HC-05 Macho
  LCD_16X2 = LCD screen
  Potenciometro = POT [package=alps_pot]  # not connected
  2kΩ = Resistor [tolerance=±5% resistance=2k package="2512 [SMD]"]
  1kΩ = Resistor [tolerance=±5% resistance=1k package="2512 [SMD]"]
  100Ω = Resistor [tolerance=±5% resistance=100 package="2512 [SMD]"]
  100Ω_2 = Resistor [tolerance=±5% resistance=100 package="2512 [SMD]"]
  NTC_10K = Temperature Sensor (Thermistor) [thermistor_type=NTC package=THT]
  10kΩ = Resistor [tolerance=±5% resistance=10k package="0603 [SMD]"]
  DHT11 = DHT11 Humitidy and Temperature Sensor

nets:
  N1: Arduino_Uno.A2, NTC_10K.pin_0, 10kΩ.Pin_0
  N2: Arduino_Uno.D11_PWM/MOSI, LCD_16X2.E
  N3: Arduino_Uno.D12/MISO, LCD_16X2.RS
  N4: Arduino_Uno.D0/RX, HC-05.TXD
  N5: Arduino_Uno.D1/TX, HC-05.RXD, 2kΩ.Pin_0, 1kΩ.Pin_1
  N6: Arduino_Uno.D2, LCD_16X2.DB7
  N7: Arduino_Uno.D3_PWM, LCD_16X2.DB6
  N8: Arduino_Uno.D4, LCD_16X2.DB5
  N9: Arduino_Uno.D5_PWM, LCD_16X2.DB4
  N10: Arduino_Uno.D6_PWM, DHT11.DATA
  VDD: Arduino_Uno.5V, HC-05.VCC, LCD_16X2.VDD, LCD_16X2.LED+, 1kΩ.Pin_0, NTC_10K.pin_1, DHT11.VDD
  GND: HC-05.GND, LCD_16X2.VSS, LCD_16X2.R/W, LCD_16X2.LED-, 10kΩ.Pin_1, DHT11.GND
  N11: 2kΩ.Pin_1, 100Ω_2.Pin_0
  N12: 100Ω.Pin_0, 100Ω_2.Pin_1

custom parts:
  DHT11 Humitidy and Temperature Sensor: DHT11 Humidity and Temperature Sensor

// code stored in the sketch: Untitled2.ino
//Made by: Crautor (Vitor Dallanol)
//Github: https://github.com/Crautor

// IMPORTAÇÃO DE BIBLIOTECAS
#include <Thermistor.h> //INCLUSÃO DA BIBLIOTECA (TEMPERATURA)
#include <SoftwareSerial.h> //INCLUSÃO DE BIBLIOTECA (BLUETOOTH)
#include <dht11.h> //INCLUSÃO DE BIBLIOTECA  DHT11 (UMIDADE)
#include <LiquidCrystal.h> //INCLUSÃOA DE BIBLIOTECA LCD (VISOR)


// DECLARAÇÃO DE VARIAVEIS
#define DHT11PIN 6 
const int pinoRX = 0; //PINO DIGITAL 0 (RX)
const int pinoTX = 1; //PINO DIGITAL 1 (TX)


// COMANDOS ESPECIFICOS DE CADA BIBLIOTECA
LiquidCrystal lcd(12,11,5,4,3,2);
dht11 DHT11;//declaração da biblioteca DHT11.H (obrigatório)
SoftwareSerial bluetooth(pinoRX, pinoTX); //PINOS QUE EMULAM A SERIAL, ONDE O PINO 0 É O RX E O PINO 1 É O TX
Thermistor temp(2); //VARIÁVEL DO TIPO THERMISTOR, INDICANDO O PINO ANALÓGICO (A2) EM QUE O TERMISTOR ESTÁ CONECTADO



void setup() {
  
  Serial.begin(9600); //INICIALIZA A SERIAL
  bluetooth.begin(9600); //INICIALIZA A SERIAL DO BLUETOOTH
  lcd.begin(16, 2); // INICIALIZA O LCD 16X2
  delay(1000); //INTERVALO DE 1 SEGUNDO
}
void loop() {
  int temperature = temp.getTemp(); //VARIÁVEL DO TIPO INTEIRO QUE RECEBE O VALOR DE TEMPERATURA CALCULADO PELA BIBLIOTECA
  int chk = DHT11.read(DHT11PIN); // VARIÁVEL DO TIPO INTEIRO QUE RECEBE O VALOR DE UMIDADE CALCULADO PELA BIBLIOTECA


  // IMPRESSÃO NO TERMINAL BLUETOOTH
  bluetooth.print("Temperatura: "); // IMPRIME O TEXTO QUE ANTECEDE A TEMPERATURA NO TERMINAL DO BLUETOOTH
  bluetooth.print(temperature); //IMPRIME A TEMPERATURA MEDIDA PELO SENSOR NO TERMINAL DO BLUETOOTH
  bluetooth.println("*C"); //IMPRIME O TEXTO QUE PRECEDE A TEMPERATURA NO TERMINAL DO BLUETOOTH
  
  bluetooth.print("Umidade (%): "); // IMPRIME O TEXTO QUE ANTECEDE A UMIDADE NO TERMINAL DO BLUETOOTH
  bluetooth.println((float)DHT11.humidity,2); // IMPRIME A UMIDADE NO TERMINAL DO BLUETOOTH


  // IMPRESSÃO NO MONITOR SERIAL
  Serial.print("Temperatura: "); //IMPRIME O TEXTO QUE ANTECEDE A TEMPERATURA NO MONITOR SERIAL
  Serial.print(temperature); //IMPRIME A TEMPERATURA MEDIDA PELO SENSOR NO MONITOR SERIAL
  Serial.println("*C"); //IMPRIME O TEXTO QUE PRECEDE A TEMPERATURA NO MONITOR SERIAL
  
  Serial.print("Umidade (%): ");// IMPRIME O TEXTO QUE ANTECEDE A UMIDADE NO MONITOR SERIAL
  Serial.println((float)DHT11.humidity,2); // IMPRIME A UMIDADE NO MONITOR SERIAL


  // IMPRESSÃO NO LCD
  lcd.clear();
  lcd.setCursor(0, 0);
  lcd.print("Temperatura:"); //IMPRIME O TEXTO QUE ANTECEDE A TEMPERATURA NO LCD
  lcd.print(temperature); //IMPRIME A TEMPERATURA MEDIDA PELO SENSOR NO LCD
  lcd.print("*C"); //IMPRIME O TEXTO QUE PRECEDE A TEMPERATURA NO LCD
  lcd.setCursor(0, 1);
  lcd.print("Umidade (%): ");// IMPRIME O TEXTO QUE ANTECEDE A UMIDADE NO LCD
  lcd.println((float)DHT11.humidity,2); // IMPRIME A UMIDADE NO LCD






  delay(1000); //INTERVALO DE 1 SEGUNDO
}
